# Fritzing sketch tunable-piezo-digitizer (saved by Fritzing 0.8.3b)
breadboards: 1

parts:
  LM393 = IC, DIP package, 8 pins [chip_label=LM393]
  D1 = Rectifier Diode [part_number=1N4001 package="300 mil [THT]"]
  D2 = Rectifier Diode [part_number=1N4001 package="300 mil [THT]"]
  trimmer = Trimmer Potentiometer [maximum_resistance=0.1MΩ package=THT]
  V1 = DC Power [voltage=5]
  piezo_sensor = Piezo Speaker
  output_(active-low) = male pin header, 1 pin [form="♂ (male)"]

nets:
  N1: LM393.pin1, output_(active-low).pin1
  N2: LM393.pin2, D1.anode, D2.cathode, piezo_sensor.pin2
  N3: LM393.pin3, trimmer.wiper
  N4: LM393.pin4, D2.anode, trimmer.leg2, V1.V-, piezo_sensor.pin1
  N5: LM393.pin8, D1.cathode, trimmer.leg1, V1.V+
